// Logisim project 7SEGMENTOS.circ as structural Verilog: 2 circuits, main circuit main
module main (
  input  in_1,
  input  in_2,
  input  in_3,
  input  in_4,
  output a,
  output b,
  output c,
  output d,
  output e,
  output f,
  output g
);

  wire and_1_out, and_2_out, and_3_out, and_4_out, and_5_out, and_6_out, and_7_out, and_8_out, and_9_out,
       and_10_out, and_11_out, and_12_out, and_13_out, and_14_out, and_15_out, and_16_out, not_1_out,
       not_2_out, not_3_out, not_4_out, not_5_out, not_6_out, not_7_out, not_8_out, not_9_out, not_10_out,
       not_11_out, not_12_out, not_13_out, not_14_out, not_15_out, not_16_out, not_17_out, not_18_out,
       not_19_out, not_20_out, not_21_out, or_1_out, or_2_out, or_3_out, or_4_out, or_5_out, or_6_out,
       or_8_out, or_11_out, or_12_out, or_14_out, or_15_out;

  not not_1 (not_1_out, in_4);
  not not_2 (not_2_out, in_2);
  not not_3 (not_3_out, in_2);
  not not_4 (not_4_out, in_4);
  not not_5 (not_5_out, in_3);
  not not_6 (not_6_out, in_4);
  not not_7 (not_7_out, in_2);
  not not_8 (not_8_out, in_4);
  not not_9 (not_9_out, in_3);
  not not_10 (not_10_out, in_4);
  not not_11 (not_11_out, in_3);
  not not_12 (not_12_out, in_4);
  not not_13 (not_13_out, in_2);
  not not_14 (not_14_out, in_4);
  not not_15 (not_15_out, in_3);
  or or_1 (or_1_out, in_1, in_3);
  and and_1 (and_1_out, in_2, in_4);
  not not_16 (not_16_out, in_2);
  and and_2 (and_2_out, not_16_out, not_17_out);
  not not_17 (not_17_out, in_4);
  not not_18 (not_18_out, in_2);
  not not_19 (not_19_out, in_3);
  and and_3 (and_3_out, not_19_out, not_20_out);
  not not_20 (not_20_out, in_4);
  and and_4 (and_4_out, in_3, in_4);
  not not_21 (not_21_out, in_3);
  or or_2 (or_2_out, not_21_out, in_4);
  or or_3 (or_3_out, in_1, and_5_out);
  and and_5 (and_5_out, in_3, not_1_out);
  and and_6 (and_6_out, not_2_out, in_3);
  and and_7 (and_7_out, not_3_out, not_4_out);
  and and_8 (and_8_out, in_2, not_5_out);
  and and_9 (and_9_out, and_8_out, in_4);
  and and_10 (and_10_out, in_3, not_6_out);
  and and_11 (and_11_out, not_7_out, not_8_out);
  or or_4 (or_4_out, in_1, and_12_out);
  and and_12 (and_12_out, not_9_out, not_10_out);
  and and_13 (and_13_out, in_2, not_11_out);
  and and_14 (and_14_out, in_2, not_12_out);
  and and_15 (and_15_out, not_13_out, in_3);
  or or_5 (or_5_out, not_14_out, not_15_out);
  or or_6 (or_6_out, or_1_out, and_1_out);
  or or_7 (a, or_6_out, and_2_out);
  or or_8 (or_8_out, not_18_out, and_3_out);
  or or_9 (b, or_8_out, and_4_out);
  or or_10 (c, or_2_out, in_2);
  or or_11 (or_11_out, or_3_out, and_6_out);
  or or_12 (or_12_out, or_11_out, and_7_out);
  or or_13 (e, and_10_out, and_11_out);
  or or_14 (or_14_out, or_4_out, and_13_out);
  or or_15 (or_15_out, in_1, and_15_out);
  or or_16 (g, or_15_out, and_16_out);
  and and_16 (and_16_out, in_2, or_5_out);
  or or_17 (d, or_12_out, and_9_out);
  or or_18 (f, or_14_out, and_14_out);

  // Notes on the sheet:
  //   a = A + C + BD + B'C'
  //   b = B' + C'D' + CD
  //   c = C' + D + B
  //   d = A + CD' + B'C + B'D' + BC'D
  //   e = CD' + B'D'
  //   f = A + C'D' + BC' + BD'
  //   g = A + B'C + BD' + B C'
  //   g = A + B'C + B(D' +C')
endmodule

module _7Seg (
  input  in_1,
  input  in_2,
  input  in_3,
  input  in_4,
  output out_5
);

  wire undriven, undriven_2, undriven_3, undriven_4, undriven_5, undriven_6, undriven_7;

  main main_1 ();  // open: in_1, in_2, in_3, in_4, a, b, c, d, e, f, g
  _7_Segment_Display u_7_segment_display_1 (
    .g(undriven_7), .f(undriven_6), .a(undriven), .b(undriven_2), .e(undriven_5), .d(undriven_4),
    .c(undriven_3));  // open: dp
endmodule
