// Logisim project ContadorSincrono.circ as structural Verilog: 1 circuit, main circuit main
module main (
);

  wire a_q, and_1_out, and_2_out, b_q, c_q, c_qn, clock_1_out, not_1_out, or_1_out;

  Clock clock_1 (.out(clock_1_out));
  J_K_Flip_Flop c (.J(and_1_out), .clk(not_1_out), .K(1'b1), .Q(c_q), .Qn(c_qn));  // open: preset, en, reset
  not not_1 (not_1_out, clock_1_out);
  and and_1 (and_1_out, a_q, b_q);
  J_K_Flip_Flop b (.J(and_2_out), .clk(not_1_out), .K(or_1_out), .Q(b_q));  // open: Qn, preset, en, reset
  or or_1 (or_1_out, c_q, a_q);
  and and_2 (and_2_out, a_q, c_qn);
  J_K_Flip_Flop a (.J(c_qn), .clk(not_1_out), .K(1'b1), .Q(a_q));  // open: Qn, preset, en, reset

  // Notes on the sheet:
  //   AB
  //   C+A
  //   AC'
endmodule
