// Logisim project Decodificador completo.circ as structural Verilog: 2 circuits, main circuit main
module main (
  input  [15:0] in_1,
  input  [3:0] in_2,
  input  [3:0] in_3,
  input  [6:0] in_4,
  input  [6:0] in_5
);

  wire decodificador_1_a_c_prime_d_prime___bc_prime_bd_prime, decodificador_1_out_5, decodificador_1_out_6,
       decodificador_1_out_7, decodificador_1_out_8, decodificador_1_out_9, decodificador_1_out_11,
       decodificador_2_a_c_prime_d_prime___bc_prime_bd_prime, decodificador_2_out_5, decodificador_2_out_6,
       decodificador_2_out_7, decodificador_2_out_8, decodificador_2_out_9, decodificador_2_out_11;

  decodificador decodificador_1 (
    .A(in_2[0]), .B(in_2[1]), .C(in_2[2]), .D(in_2[3]), .out_5(decodificador_1_out_5),
    .out_6(decodificador_1_out_6), .out_7(decodificador_1_out_7), .out_8(decodificador_1_out_8),
    .out_9(decodificador_1_out_9),
    .A_C_prime_D_prime___BC_prime_BD_prime(decodificador_1_a_c_prime_d_prime___bc_prime_bd_prime),
    .out_11(decodificador_1_out_11));
  decodificador decodificador_2 (
    .A(in_3[0]), .B(in_3[1]), .C(in_3[2]), .D(in_3[3]), .out_5(decodificador_2_out_5),
    .out_6(decodificador_2_out_6), .out_7(decodificador_2_out_7), .out_8(decodificador_2_out_8),
    .out_9(decodificador_2_out_9),
    .A_C_prime_D_prime___BC_prime_BD_prime(decodificador_2_a_c_prime_d_prime___bc_prime_bd_prime),
    .out_11(decodificador_2_out_11));
  _7_Segment_Display #(.active("false")) u_7_segment_display_1 (
    .g(in_4[4]), .f(in_4[3]), .a(in_4[0]), .b(in_4[1]), .e(in_4[5]), .d(in_4[6]), .c(in_4[2]), .dp(1'b1));
  _7_Segment_Display u_7_segment_display_2 (
    .g(decodificador_1_out_11), .f(decodificador_1_a_c_prime_d_prime___bc_prime_bd_prime),
    .a(decodificador_1_out_5), .b(decodificador_1_out_6), .e(decodificador_1_out_9),
    .d(decodificador_1_out_8), .c(decodificador_1_out_7));  // open: dp
  _7_Segment_Display u_7_segment_display_3 (
    .g(decodificador_2_out_11), .f(decodificador_2_a_c_prime_d_prime___bc_prime_bd_prime),
    .a(decodificador_2_out_5), .b(decodificador_2_out_6), .e(decodificador_2_out_9),
    .d(decodificador_2_out_8), .c(decodificador_2_out_7));  // open: dp
  _7_Segment_Display #(.active("false")) u_7_segment_display_4 (
    .g(in_5[4]), .f(in_5[3]), .a(in_5[0]), .b(in_5[1]), .e(in_5[5]), .d(in_5[6]), .c(in_5[2]), .dp(1'b1));
endmodule

module decodificador (
  input  A,
  input  B,
  input  C,
  input  D,
  output out_5,
  output out_6,
  output out_7,
  output out_8,
  output out_9,
  output A_C_prime_D_prime___BC_prime_BD_prime,
  output out_11
);

  wire and_1_out, and_2_out, and_3_out, and_4_out, and_5_out, and_6_out, and_7_out, and_8_out, and_9_out,
       and_10_out, and_11_out, and_12_out, and_13_out, and_14_out, and_15_out, and_16_out;

  and and_1 (and_1_out, B, ~C, D);  // AND_Gate
  and and_2 (and_2_out, ~B, C);  // AND_Gate
  and and_3 (and_3_out, C, ~D);  // AND_Gate
  and and_4 (and_4_out, ~B, ~D);  // AND_Gate
  and and_5 (and_5_out, ~B, ~D);  // AND_Gate
  and and_6 (and_6_out, C, ~D);  // AND_Gate
  and and_7 (and_7_out, ~C, ~D);  // AND_Gate
  and and_8 (and_8_out, B, ~C);  // AND_Gate
  and and_9 (and_9_out, B, ~D);  // AND_Gate
  and and_10 (and_10_out, C, ~D);  // AND_Gate
  and and_11 (and_11_out, B, ~C);  // AND_Gate
  and and_12 (and_12_out, ~B, C);  // AND_Gate
  or or_1 (out_8, and_1_out, and_2_out, and_3_out, and_4_out);
  or or_2 (out_9, and_5_out, and_6_out);
  or or_3 (A_C_prime_D_prime___BC_prime_BD_prime, A, and_7_out, and_8_out, and_9_out);
  and and_13 (and_13_out, B, D);
  and and_14 (and_14_out, ~B, ~D);  // AND_Gate
  and and_15 (and_15_out, C, D);
  and and_16 (and_16_out, ~C, ~D);  // AND_Gate
  or or_4 (out_11, A, and_10_out, and_11_out, and_12_out);
  or or_5 (out_6, and_15_out, and_16_out, ~B);  // OR_Gate
  or or_6 (out_7, ~C, D, B);  // OR_Gate
  or or_7 (out_5, A, and_13_out, C, and_14_out);

  // Notes on the sheet:
  //   A+B'+D'+C.D'+B'C+BC'D
  //   B'D'+CD'
  //   B'+C'D'+CD
  //   C'+D+B
  //   A+C+B.D+B'D'
endmodule
