// Logisim project MaquinaEstados.circ as structural Verilog: 1 circuit, main circuit main
module main (
  input  Entrada,
  input  clk,
  output out_3
);

  wire and_1_out, and_2_out, and_3_out, not_1_out, or_1_out, or_2_out, q0_q, q1_q;

  not not_1 (not_1_out, q0_q);
  and and_1 (and_1_out, not_1_out, Entrada);
  or or_1 (or_1_out, and_1_out, and_2_out);
  and and_2 (and_2_out, Entrada, q1_q);
  and and_3 (and_3_out, Entrada, q0_q);
  or or_2 (or_2_out, and_2_out, and_3_out);
  D_Flip_Flop q1 (.clk(clk), .D(or_2_out), .Q(q1_q));  // open: Qn, preset, en, reset
  and and_4 (out_3, q1_q, q0_q);
  D_Flip_Flop q0 (.clk(clk), .D(or_1_out), .Q(q0_q));  // open: Qn, preset, en, reset
endmodule
