// Logisim project SOMADOR.circ as structural Verilog: 2 circuits, main circuit somador
module somador (
  input  A,
  input  B,
  input  CarryIn,
  output carryOut,
  output Sum
);

  wire and_1_out, and_2_out, xor_1_out;

  or or_1 (carryOut, and_1_out, and_2_out);
  and and_1 (and_1_out, A, B);
  and and_2 (and_2_out, CarryIn, xor_1_out);
  xor xor_1 (xor_1_out, A, B);
  xor xor_2 (Sum, CarryIn, xor_1_out);

  // Notes on the sheet:
  //   carry das entradas
  //   carry do carry in
endmodule

module Somador_4_bits (
  input  a3,
  input  b3,
  input  a2,
  input  b2,
  input  a1,
  input  b1,
  input  a0,
  input  b0,
  input  Sub,
  output CarryOut,
  output s3,
  output s2,
  output s1,
  output s0
);

  wire somador_2_carryout, somador_3_carryout, somador_4_carryout, xor_1_out, xor_2_out, xor_3_out, xor_4_out;

  xor xor_1 (xor_1_out, b3, Sub);
  somador somador_1 (.carryOut(CarryOut), .A(a3), .B(xor_1_out), .Sum(s3), .CarryIn(somador_2_carryout));
  xor xor_2 (xor_2_out, b2, Sub);
  somador somador_2 (.carryOut(somador_2_carryout), .A(a2), .B(xor_2_out), .Sum(s2), .CarryIn(somador_3_carryout));
  somador somador_3 (.carryOut(somador_3_carryout), .A(a1), .B(xor_3_out), .Sum(s1), .CarryIn(somador_4_carryout));
  xor xor_3 (xor_3_out, b1, Sub);
  xor xor_4 (xor_4_out, b0, Sub);
  somador somador_4 (.carryOut(somador_4_carryout), .A(a0), .B(xor_4_out), .Sum(s0), .CarryIn(Sub));

  // Notes on the sheet:
  //   tirar o carry se for sub?
endmodule
