// Logisim project sequenciais.circ as structural Verilog: 2 circuits, main circuit main
module main (
  input  crescente
);

  wire _10_out, _15_out, and_1_out, and_2_out, and_3_out, and_4_out, and_5_out, clock_1_out, j_k_ff_1_q,
       j_k_ff_2_q, j_k_ff_3_q, j_k_ff_4_q, main_1_a, main_1_b, main_1_c, main_1_d, main_1_e, main_1_f,
       main_1_g, not_1_out, not_2_out, not_3_out, or_1_out, undriven, xor_1_out, xor_2_out, xor_3_out,
       xor_4_out;

  Clock clock_1 (.out(clock_1_out));
  Clock clock_2 ();  // open: out
  not not_1 (not_1_out, clock_1_out);
  and and_1 (and_1_out, not_1_out, _15_out);
  and and_2 (and_2_out, not_1_out, or_1_out);
  and and_3 (and_3_out, not_1_out, _10_out);
  J_K_Flip_Flop j_k_ff_1 (
    .J(1'b1), .clk(clock_1_out), .K(1'b1), .Q(j_k_ff_1_q), .preset(and_1_out), .reset(and_3_out));  // open: Qn, en
  xor xor_1 (xor_1_out, crescente, j_k_ff_1_q);
  _7SEGMENTOS_main main_1 (
    .in_1(xor_4_out), .in_2(xor_3_out), .in_3(xor_2_out), .in_4(xor_1_out), .a(main_1_a), .b(main_1_b),
    .c(main_1_c), .d(main_1_d), .e(main_1_e), .f(main_1_f), .g(main_1_g));
  J_K_Flip_Flop j_k_ff_2 (
    .J(1'b1), .clk(j_k_ff_1_q), .K(1'b1), .Q(j_k_ff_2_q), .reset(and_2_out));  // open: Qn, preset, en
  xor xor_2 (xor_2_out, crescente, j_k_ff_2_q);
  _7_Segment_Display u_7_segment_display_1 (
    .g(main_1_g), .f(main_1_f), .a(main_1_a), .b(main_1_b), .e(main_1_e), .d(main_1_d), .c(main_1_c));  // open: dp
  J_K_Flip_Flop j_k_ff_3 (
    .J(1'b1), .clk(j_k_ff_2_q), .K(1'b1), .Q(j_k_ff_3_q), .reset(and_2_out));  // open: Qn, preset, en
  and and_4 (and_4_out, xor_3_out, xor_2_out);
  not not_2 (not_2_out, xor_3_out);
  and and_5 (and_5_out, not_2_out, xor_2_out);
  xor xor_3 (xor_3_out, crescente, j_k_ff_3_q);
  and _15 (_15_out, xor_4_out, and_4_out, xor_1_out);
  and _10 (_10_out, xor_4_out, and_5_out, not_3_out);
  not not_3 (not_3_out, xor_1_out);
  J_K_Flip_Flop j_k_ff_4 (
    .J(1'b1), .clk(j_k_ff_3_q), .K(1'b1), .Q(j_k_ff_4_q), .preset(and_1_out), .en(undriven), .reset(undriven));  // open: Qn
  xor xor_4 (xor_4_out, crescente, j_k_ff_4_q);
  or or_1 (or_1_out, _15_out, _10_out);

  // Notes on the sheet:
  //   limite = 1111 -> 1001  ou 1010 -> 0000
endmodule

module sincronizador_4freq (
  input  in_1,
  output out_2
);

  wire d_ff_1_q, d_ff_2_q, d_ff_3_q;

  D_Flip_Flop d_ff_1 (.clk(in_1), .D(in_1), .Q(d_ff_1_q), .reset(out_2));  // open: Qn, preset, en
  D_Flip_Flop d_ff_2 (.clk(in_1), .D(d_ff_1_q), .Q(d_ff_2_q), .reset(out_2));  // open: Qn, preset, en
  D_Flip_Flop d_ff_3 (.clk(in_1), .D(d_ff_2_q), .Q(d_ff_3_q), .reset(out_2));  // open: Qn, preset, en
  D_Flip_Flop d_ff_4 (.clk(in_1), .D(d_ff_3_q), .Q(out_2), .reset(out_2));  // open: Qn, preset, en
endmodule
